# Fritzing sketch Modem_Microduino (saved by Fritzing 0.8.5b)
circuit board: 2.72191cm x 2.46083cm
breadboards: 2

parts:
  R1 = Resistor [tolerance=±1% resistance=1k package=THT]
  R2 = Resistor [tolerance=±1% resistance=2.2k package=THT]
  R3 = Resistor [tolerance=±1% resistance=3.9k package=THT]
  C1 = Electrolytic Capacitor [capacitance=4.7µF voltage=50V package="100 mil [THT, electrolytic]"]
  C2 = Ceramic Capacitor [capacitance=100nF package="100 mil [THT, multilayer]"]
  R5 = Resistor [tolerance=±5% resistance=270 package=THT]
  OUT = female pin header, 1 pin [form="♀ (female)"]
  R_MODOUT_VDIV1 = Resistor [tolerance=±5% resistance=100k package=THT]
  R_MODOUT_VDIV2 = Resistor [tolerance=±5% resistance=1k package=THT]
  IN = female pin header, 1 pin [form="♀ (female)"]
  GND = female pin header, 1 pin [form="♀ (female)"]
  C3 = Ceramic Capacitor [capacitance=1µF package="100 mil [THT, multilayer]"]
  RB1 = Resistor [tolerance=±5% resistance=100k package=THT]
  RB2 = Resistor [tolerance=±5% resistance=100k package=THT]
  RG = Resistor [tolerance=±5% resistance=10k package=THT]
  PTT = female pin header, 1 pin [form="♀ (female)"]
  PTT+ = female pin header, 1 pin [form="♀ (female)"]
  Microduino_Left = MicroduinoUPin3 [form="♀ (female)" package=THT]
  MicroDuino_Top = MicroduinoUPin1 [form="♀ (female)" package=THT]
  R4 = Resistor [tolerance=±1% resistance=8.2k package=THT]
  RX = LED - 3mm [color="Green (570nm)" package="3 mm [THT]"]
  TX = LED - 3mm [color="Blue (505nm)" package="3 mm [THT]"]
  N_MOSFET_PTT = MOSFET-NCHANNEL [package=to-92]
  Microduino_Bottom = Generic female header - 6 pins [form="♀ (female)" package=THT]
  R6 = Resistor [tolerance=±5% resistance=220 package=THT]
  LINE-LEVEL_OUT = female pin header, 1 pin [form="♀ (female)"]
  A1 = female pin header, 1 pin [form="♀ (female)"]  # not connected

nets (from the schematic view):
  N1: R1.Pin_0, Microduino_Bottom.D7
  N2: R1.Pin_1, R2.Pin_1, R3.Pin_1, C1.-, C2.1, R5.Pin_0, R4.Pin_1
  N3: R2.Pin_0, MicroDuino_Top.D6
  N4: R3.Pin_0, MicroDuino_Top.D5
  N5: C1.+, LINE-LEVEL_OUT.pin1
  N6: C2.0, R5.Pin_1
  N7: OUT.pin1, R_MODOUT_VDIV1.Pin_0, R_MODOUT_VDIV2.Pin_1
  GND: R_MODOUT_VDIV2.Pin_0, GND.pin1, RB2.Pin_1, RG.Pin_1, MicroDuino_Top.GND, R6.Pin_1
  N8: IN.pin1, C3.1
  N9: C3.0, RB1.Pin_0, RB2.Pin_0, Microduino_Left.A0
  N10: RB1.Pin_1, Microduino_Bottom.5V
  N11: RG.Pin_0, MicroDuino_Top.D3, N_MOSFET_PTT.G
  N12: PTT.pin1, N_MOSFET_PTT.S
  N13: PTT+.pin1, N_MOSFET_PTT.D
  N14: MicroDuino_Top.D4, R4.Pin_0
  N15: RX.cathode, TX.cathode, R6.Pin_0
  N16: RX.anode, Microduino_Bottom.D10
  N17: TX.anode, Microduino_Bottom.D9

notes:
  This breadboard represents the pins on the Microduino.
  RX/TX LEDs
  MOSFET for keying a radio's PTT
  +2.5v bias for ADC input
  4-bit resistor ladder DAC
  This voltage divider brings the output down to MIC level.
  This tap provides line-level output

custom parts:
  MicroduinoUPin3: Microduino Upin
  MicroduinoUPin1: Microduino Upin
  Generic female header - 6 pins: Generic female header
